// Logisim project Decoders.circ as structural Verilog: 4 circuits, main circuit dec24
module dec24 (
  input  En,
  input  A,
  input  B,
  output Y0,
  output Y1,
  output Y2,
  output Y3
);

  wire not_1_out, not_2_out;

  not not_1 (not_1_out, A);
  not not_2 (not_2_out, B);
  and and_1 (Y0, not_1_out, not_2_out, En);
  and and_2 (Y1, not_1_out, B, En);
  and and_3 (Y2, A, not_2_out, En);
  and and_4 (Y3, A, B, En);
endmodule

module dec38 (
  input  En,
  input  A,
  input  B,
  input  C,
  output Y0,
  output Y1,
  output Y2,
  output Y3,
  output Y4,
  output Y5,
  output Y6,
  output Y7
);

  wire not_1_out, not_2_out, not_3_out, not_4_out, not_5_out, not_6_out, not_7_out, not_8_out, not_9_out,
       not_10_out, not_11_out, not_12_out;

  not not_1 (not_1_out, A);
  not not_2 (not_2_out, B);
  not not_3 (not_3_out, C);
  not not_4 (not_4_out, A);
  not not_5 (not_5_out, B);
  not not_6 (not_6_out, A);
  not not_7 (not_7_out, C);
  not not_8 (not_8_out, A);
  not not_9 (not_9_out, B);
  not not_10 (not_10_out, C);
  not not_11 (not_11_out, B);
  not not_12 (not_12_out, C);
  and and_1 (Y7, En, A, B, C);
  and and_2 (Y0, En, not_1_out, not_2_out, not_3_out);
  and and_3 (Y1, En, not_4_out, not_5_out, C);
  and and_4 (Y2, En, not_6_out, B, not_7_out);
  and and_5 (Y3, En, not_8_out, B, C);
  and and_6 (Y4, En, A, not_9_out, not_10_out);
  and and_7 (Y5, En, A, not_11_out, C);
  and and_8 (Y6, En, A, B, not_12_out);
endmodule

module dec4to16 (
  input  En,
  input  A,
  input  B,
  input  C,
  input  D,
  output Y0,
  output Y1,
  output Y2,
  output Y3,
  output Y4,
  output Y5,
  output Y6,
  output Y7,
  output Y8,
  output Y9,
  output Y10,
  output Y11,
  output Y12,
  output Y13,
  output Y14,
  output Y15
);

  wire dec38_1_y0, dec38_1_y1, dec38_1_y2, dec38_1_y3, dec38_1_y4, dec38_1_y5, dec38_1_y6, dec38_1_y7,
       dec38_2_y0, dec38_2_y1, dec38_2_y2, dec38_2_y3, dec38_2_y4, dec38_2_y5, dec38_2_y6, dec38_2_y7,
       not_1_out, not_2_out;

  not not_1 (not_1_out, A);
  not not_2 (not_2_out, not_1_out);
  dec38 dec38_1 (
    .En(not_1_out), .Y0(dec38_1_y0), .A(B), .B(C), .Y1(dec38_1_y1), .C(D), .Y2(dec38_1_y2), .Y3(dec38_1_y3),
    .Y4(dec38_1_y4), .Y5(dec38_1_y5), .Y6(dec38_1_y6), .Y7(dec38_1_y7));
  dec38 dec38_2 (
    .En(not_2_out), .Y0(dec38_2_y0), .A(B), .B(C), .Y1(dec38_2_y1), .C(D), .Y2(dec38_2_y2), .Y3(dec38_2_y3),
    .Y4(dec38_2_y4), .Y5(dec38_2_y5), .Y6(dec38_2_y6), .Y7(dec38_2_y7));
  and and_1 (Y0, En, dec38_1_y0);
  and and_2 (Y2, dec38_1_y2, En);
  and and_3 (Y4, dec38_1_y4, En);
  and and_4 (Y6, dec38_1_y6, En);
  and and_5 (Y8, dec38_2_y0, En);
  and and_6 (Y10, dec38_2_y2, En);
  and and_7 (Y12, dec38_2_y4, En);
  and and_8 (Y14, dec38_2_y6, En);
  and and_9 (Y1, dec38_1_y1, En);
  and and_10 (Y3, dec38_1_y3, En);
  and and_11 (Y5, dec38_1_y5, En);
  and and_12 (Y7, dec38_1_y7, En);
  and and_13 (Y9, dec38_2_y1, En);
  and and_14 (Y11, dec38_2_y3, En);
  and and_15 (Y13, dec38_2_y5, En);
  and and_16 (Y15, dec38_2_y7, En);
endmodule

module Bool_dec38 (
  input  En,
  input  A,
  input  B,
  output Y_minterms,
  output Y_minterms_br
);

  wire dec24_1_y0, dec24_1_y1, dec24_1_y2, dec24_1_y3;

  dec24 dec24_1 (.En(En), .A(A), .B(B), .Y0(dec24_1_y0), .Y1(dec24_1_y1), .Y2(dec24_1_y2), .Y3(dec24_1_y3));
  or or_1 (Y_minterms, dec24_1_y0, dec24_1_y2);
  nor nor_1 (Y_minterms_br, dec24_1_y1, dec24_1_y3);
endmodule
