// Logisim project Flipflops.circ as structural Verilog: 6 circuits, main circuit basic_bistable
module basic_bistable (
  input  in_1,
  input  in_2,
  output out_3,
  output out_4
);

  not not_1 (in_2, in_1);
  not not_2 (in_1, in_2);

  assign out_3 = in_2;
  assign out_4 = in_1;
endmodule

module SR_latch (
  input  S,
  input  En,
  input  R,
  output Q,
  output Qb
);

  wire nand_1_out, nand_2_out;

  nand nand_1 (nand_1_out, S, En);
  nand nand_2 (nand_2_out, En, R);
  nand nand_3 (Q, nand_1_out, Qb);
  nand nand_4 (Qb, Q, nand_2_out);
endmodule

module D_latch (
  input  D,
  input  En,
  output Qb,
  output Q
);

  wire nand_1_out, nand_2_out, not_1_out;

  not not_1 (not_1_out, D);
  nand nand_1 (nand_1_out, D, En);
  nand nand_2 (nand_2_out, En, not_1_out);
  nand nand_3 (Qb, nand_1_out, Q);
  nand nand_4 (Q, Qb, nand_2_out);
endmodule

module MS_SR (
  input  S,
  input  R,
  input  Pr,
  input  Clr,
  output out_5,
  output out_6
);

  wire Clk_out, not_1_out, s_r_ff_1_q, s_r_ff_1_qn;

  Clock Clk (.out(Clk_out));
  S_R_Flip_Flop s_r_ff_1 (
    .S(S), .clk(Clk_out), .R(R), .Q(s_r_ff_1_q), .Qn(s_r_ff_1_qn), .preset(Pr), .reset(Clr));  // open: en
  not not_1 (not_1_out, Clk_out);
  S_R_Flip_Flop s_r_ff_2 (
    .S(s_r_ff_1_q), .clk(not_1_out), .R(s_r_ff_1_qn), .Q(out_5), .Qn(out_6), .preset(Pr), .reset(Clr));  // open: en
endmodule

module SR_no_En (
  input  S,
  input  R,
  output Qb,
  output Q
);

  nand nand_1 (Qb, S, Q);
  nand nand_2 (Q, Qb, R);
endmodule

module MS_JK (
  input  J,
  input  K,
  output out_3,
  output out_4
);

  wire and_1_out, and_2_out, Clk_out, not_1_out, s_r_ff_1_q, s_r_ff_1_qn;

  Clock Clk (.out(Clk_out));
  and and_1 (and_1_out, out_4, J);
  and and_2 (and_2_out, K, out_3);
  S_R_Flip_Flop s_r_ff_1 (
    .S(and_1_out), .clk(Clk_out), .R(and_2_out), .Q(s_r_ff_1_q), .Qn(s_r_ff_1_qn));  // open: preset, reset, en
  not not_1 (not_1_out, Clk_out);
  S_R_Flip_Flop s_r_ff_2 (
    .S(s_r_ff_1_q), .clk(not_1_out), .R(s_r_ff_1_qn), .Q(out_3), .Qn(out_4));  // open: preset, reset, en
endmodule
