// Logisim project Adders.circ as structural Verilog: 6 circuits, main circuit par_addr_sub
module main (
  input  [3:0] B,
  input  Cin,
  input  [3:0] A,
  output [3:0] Sum,
  output Cout
);

  wire full_adder_2_carry, full_adder_3_carry, full_adder_4_carry;

  full_adder full_adder_1 (.A(full_adder_2_carry), .B(B[3]), .C(A[3]), .Sum(Sum[3]), .Carry(Cout));
  full_adder full_adder_2 (.A(full_adder_3_carry), .B(B[2]), .C(A[2]), .Sum(Sum[2]), .Carry(full_adder_2_carry));
  full_adder full_adder_3 (.A(full_adder_4_carry), .B(B[1]), .C(A[1]), .Sum(Sum[1]), .Carry(full_adder_3_carry));
  full_adder full_adder_4 (.A(Cin), .B(B[0]), .C(A[0]), .Sum(Sum[0]), .Carry(full_adder_4_carry));
endmodule

module full_adder (
  input  A,
  input  B,
  input  C,
  output Sum,
  output Carry
);

  wire half_adder_1_carry, half_adder_1_sum, half_adder_2_carry;

  half_adder half_adder_1 (.A(A), .B(B), .Sum(half_adder_1_sum), .Carry(half_adder_1_carry));
  half_adder half_adder_2 (.A(half_adder_1_sum), .B(C), .Sum(Sum), .Carry(half_adder_2_carry));
  or or_1 (Carry, half_adder_2_carry, half_adder_1_carry);
endmodule

module half_adder (
  input  A,
  input  B,
  output Sum,
  output Carry
);

  xor xor_1 (Sum, A, B);
  and and_1 (Carry, A, B);
endmodule

module par_addr_sub (
  input  [3:0] A,
  input  Sub_Addbr,
  input  [3:0] B,
  output out_4,
  output [3:0] out_5
);

  wire [3:0] ones_comp_1_acomp;

  ones_comp ones_comp_1 (.comp(Sub_Addbr), .A(B), .Acomp(ones_comp_1_acomp));
  main main_1 (.B(A), .A(ones_comp_1_acomp), .Cout(out_4), .Cin(Sub_Addbr), .Sum(out_5));
endmodule

module ones_comp (
  input  comp,
  input  [3:0] A,
  output [3:0] Acomp
);

  xor xor_1 (Acomp[0], comp, A[0]);
  xor xor_2 (Acomp[1], comp, A[1]);
  xor xor_3 (Acomp[2], comp, A[2]);
  xor xor_4 (Acomp[3], comp, A[3]);
endmodule

module BCD_Adder (
);

  wire and_1_out, and_2_out, main_1_cout, or_1_out;
  wire [3:0] main_1_sum;

  main main_1 (.Cout(main_1_cout), .Sum(main_1_sum));  // open: B, A, Cin
  and and_1 (and_1_out, main_1_sum[1], main_1_sum[3]);
  and and_2 (and_2_out, main_1_sum[3], main_1_sum[2]);
  or or_1 (or_1_out, main_1_cout, and_1_out, and_2_out);
  main main_2 ();  // open: B, A, Cout, Cin, Sum
endmodule
