// Logisim project Encoders.circ as structural Verilog: 2 circuits, main circuit encoder
module encoder (
  input  x0,
  input  x1,
  input  x2,
  input  x3,
  input  x4,
  input  x5,
  input  x6,
  input  x7,
  output z0,
  output z1,
  output z2
);

  or or_1 (z0, x1, x3, x5, x7);
  or or_2 (z1, x2, x3, x6, x7);
  or or_3 (z2, x4, x5, x6, x7);
endmodule

module pri_enc38 (
  input  x0,
  input  x1,
  input  x2,
  input  x3,
  input  x4,
  input  x5,
  input  x6,
  input  x7,
  input  en,
  output z0,
  output z1,
  output z2
);

  Priority_Encoder priority_encoder_1 (
    .in0(x0), .in1(x1), .in2(x2), .in3(x3), .in4(x4), .in5(x5), .in6(x6), .in7(x7), .out({z2, z1, z0}),
    .en_in(en), .en_out(en));  // open: gs
endmodule
