// Logisim project Mux.circ as structural Verilog: 2 circuits, main circuit mux24
module mux24 (
  input  E,
  input  S1,
  input  S0,
  input  I0,
  input  I1,
  input  I2,
  input  I3,
  output Y
);

  wire and_1_out, and_2_out, and_3_out, and_4_out, not_1_out, not_2_out, not_3_out, not_4_out, or_1_out;

  not not_1 (not_1_out, S1);
  not not_2 (not_2_out, S0);
  not not_3 (not_3_out, S1);
  not not_4 (not_4_out, S0);
  and and_1 (and_1_out, I0, not_1_out, not_2_out);
  and and_2 (and_2_out, I1, not_3_out, S0);
  and and_3 (and_3_out, I2, S1, not_4_out);
  and and_4 (and_4_out, I3, S1, S0);
  or or_1 (or_1_out, and_1_out, and_2_out, and_3_out, and_4_out);
  and and_5 (Y, E, or_1_out);
endmodule

module mux16to1 (
  input  En,
  input  [3:0] s3s2s1s0,
  input  [15:0] x0_to_x16,
  output Y
);

  wire mux24_1_y, mux24_2_y, mux24_3_y, mux24_4_y;

  mux24 mux24_1 (
    .E(En), .S1(s3s2s1s0[1]), .S0(s3s2s1s0[0]), .I1(x0_to_x16[1]), .I0(x0_to_x16[0]), .I2(x0_to_x16[2]),
    .I3(x0_to_x16[3]), .Y(mux24_1_y));
  mux24 mux24_2 (
    .E(En), .S1(s3s2s1s0[1]), .S0(s3s2s1s0[0]), .I1(x0_to_x16[5]), .I0(x0_to_x16[4]), .I2(x0_to_x16[6]),
    .I3(x0_to_x16[7]), .Y(mux24_2_y));
  mux24 mux24_3 (
    .E(En), .S1(s3s2s1s0[1]), .S0(s3s2s1s0[0]), .I1(x0_to_x16[9]), .I0(x0_to_x16[8]), .I2(x0_to_x16[10]),
    .I3(x0_to_x16[11]), .Y(mux24_3_y));
  mux24 mux24_4 (
    .E(En), .S1(s3s2s1s0[1]), .S0(s3s2s1s0[0]), .I1(x0_to_x16[13]), .I0(x0_to_x16[12]), .I2(x0_to_x16[14]),
    .I3(x0_to_x16[15]), .Y(mux24_4_y));
  mux24 mux24_5 (
    .E(En), .S1(s3s2s1s0[3]), .S0(s3s2s1s0[2]), .I1(mux24_2_y), .I0(mux24_1_y), .I2(mux24_3_y),
    .I3(mux24_4_y), .Y(Y));
endmodule
