// Logisim project counters.circ as structural Verilog: 4 circuits, main circuit Binary_Ripple_Counter
module Binary_Ripple_Counter (
  input  Count_en,
  output [3:0] out_2
);

  wire and_1_out, and_2_out, and_3_out, Clock_out;

  Clock Clock (.out(Clock_out));
  T_Flip_Flop t_ff_1 (.clk(Clock_out), .T(Count_en), .Q(out_2[0]), .en(1'b1));  // open: Qn, preset, reset
  and and_1 (and_1_out, out_2[0], Count_en);
  T_Flip_Flop t_ff_2 (.clk(Clock_out), .T(and_1_out), .Q(out_2[1]), .en(1'b1));  // open: Qn, preset, reset
  and and_2 (and_2_out, out_2[1], out_2[0], Count_en);
  T_Flip_Flop t_ff_3 (.clk(Clock_out), .T(and_2_out), .Q(out_2[2]), .en(1'b1));  // open: Qn, preset, reset
  and and_3 (and_3_out, out_2[1], out_2[2], out_2[0], Count_en);
  T_Flip_Flop t_ff_4 (.clk(Clock_out), .T(and_3_out), .Q(out_2[3]), .en(1'b1));  // open: Qn, preset, reset
endmodule

module ripple_counter (
  input  Count_en,
  output [3:0] out_2
);

  wire and_1_out, and_2_out, and_3_out, Clock_out;

  Clock Clock (.out(Clock_out));
  T_Flip_Flop t_ff_1 (.clk(Clock_out), .T(Count_en), .Q(out_2[0]), .en(1'b1));  // open: Qn, preset, reset
  and and_1 (and_1_out, out_2[0], Count_en);
  T_Flip_Flop t_ff_2 (.clk(Clock_out), .T(and_1_out), .Q(out_2[1]), .en(1'b1));  // open: Qn, preset, reset
  and and_2 (and_2_out, out_2[1], and_1_out);
  T_Flip_Flop t_ff_3 (.clk(Clock_out), .T(and_2_out), .Q(out_2[2]), .en(1'b1));  // open: Qn, preset, reset
  and and_3 (and_3_out, out_2[2], and_2_out);
  T_Flip_Flop t_ff_4 (.clk(Clock_out), .T(and_3_out), .Q(out_2[3]), .en(1'b1));  // open: Qn, preset, reset
endmodule

module SpecialCounter (
  output [2:0] out_1
);

  wire and_1_out, and_2_out, and_3_out, and_4_out, Clock_out, or_1_out, or_2_out, t_ff_1_qn, t_ff_2_qn,
       t_ff_3_qn;

  Clock Clock (.out(Clock_out));
  and and_1 (and_1_out, out_1[2], t_ff_2_qn, t_ff_1_qn);
  T_Flip_Flop t_ff_1 (.clk(Clock_out), .T(and_1_out), .Q(out_1[0]), .Qn(t_ff_1_qn), .en(1'b1));  // open: preset, reset
  and and_2 (and_2_out, t_ff_3_qn, t_ff_2_qn);
  T_Flip_Flop t_ff_2 (.clk(Clock_out), .T(or_1_out), .Q(out_1[1]), .Qn(t_ff_2_qn), .en(1'b1));  // open: preset, reset
  or or_1 (or_1_out, and_2_out, out_1[0]);
  T_Flip_Flop t_ff_3 (.clk(Clock_out), .T(or_2_out), .Q(out_1[2]), .Qn(t_ff_3_qn), .en(1'b1));  // open: preset, reset
  and and_3 (and_3_out, out_1[2], t_ff_2_qn);
  and and_4 (and_4_out, t_ff_3_qn, out_1[1]);
  or or_2 (or_2_out, and_3_out, and_4_out);
endmodule

module mod6_JK (
  output [2:0] out_1
);

  wire and_1_out, and_2_out, and_3_out, and_4_out, and_5_out, Clock_out, d_ff_1_qn, d_ff_2_qn, d_ff_3_qn,
       or_1_out, or_2_out, or_3_out;

  Clock Clock (.out(Clock_out));
  and and_1 (and_1_out, out_1[2], out_1[1]);
  and and_2 (and_2_out, out_1[1], out_1[0]);
  or or_1 (or_1_out, and_1_out, and_2_out);
  D_Flip_Flop d_ff_1 (.clk(Clock_out), .D(or_1_out), .Q(out_1[2]), .Qn(d_ff_1_qn), .en(1'b1));  // open: preset, reset
  and and_3 (and_3_out, d_ff_1_qn, out_1[1]);
  and and_4 (and_4_out, d_ff_2_qn, d_ff_3_qn);
  D_Flip_Flop d_ff_2 (.clk(Clock_out), .D(or_2_out), .Q(out_1[1]), .Qn(d_ff_2_qn), .en(1'b1));  // open: preset, reset
  or or_2 (or_2_out, and_3_out, and_4_out);
  D_Flip_Flop d_ff_3 (.clk(Clock_out), .D(or_3_out), .Q(out_1[0]), .Qn(d_ff_3_qn), .en(1'b1));  // open: preset, reset
  and and_5 (and_5_out, out_1[2], out_1[1]);
  or or_3 (or_3_out, and_5_out, d_ff_3_qn);
endmodule
