// Logisim project shift_reg.circ as structural Verilog: 4 circuits, main circuit SISO
module SISO (
  input  Ser_data_in,
  output Q2,
  output Q1,
  output Q0_Ser_DataOut
);

  wire clock_1_out;

  Clock clock_1 (.out(clock_1_out));
  D_Flip_Flop d_ff_1 (.clk(clock_1_out), .D(Ser_data_in), .Q(Q2));  // open: Qn, preset, en, reset
  D_Flip_Flop d_ff_2 (.clk(clock_1_out), .D(Q2), .Q(Q1));  // open: Qn, preset, en, reset
  D_Flip_Flop d_ff_3 (.clk(clock_1_out), .D(Q1), .Q(Q0_Ser_DataOut));  // open: Qn, preset, en, reset
endmodule

module SIPO (
  input  Ser_data_in,
  output Q3,
  output Q2,
  output Q1,
  output Q0
);

  wire clock_1_out;

  Clock clock_1 (.out(clock_1_out));
  D_Flip_Flop d_ff_1 (.clk(clock_1_out), .D(Ser_data_in), .Q(Q3));  // open: Qn, preset, en, reset
  D_Flip_Flop d_ff_2 (.clk(clock_1_out), .D(Q3), .Q(Q2));  // open: Qn, preset, en, reset
  D_Flip_Flop d_ff_3 (.clk(clock_1_out), .D(Q2), .Q(Q1));  // open: Qn, preset, en, reset
  D_Flip_Flop d_ff_4 (.clk(clock_1_out), .Q(Q0));  // open: D, Qn, preset, en, reset
endmodule

module PISO (
  input  Ser_data_in,
  input  LdBr_Shft,
  input  I3,
  input  I2,
  input  I1,
  input  I0,
  output Q3,
  output Q2,
  output Q1,
  output Q0,
  output Serial_dataOut
);

  wire and_1_out, and_2_out, and_3_out, and_4_out, and_5_out, and_6_out, and_7_out, and_8_out, clock_1_out,
       not_1_out, or_1_out, or_2_out, or_3_out, or_4_out;

  Clock clock_1 (.out(clock_1_out));
  not not_1 (not_1_out, LdBr_Shft);
  and and_1 (and_1_out, Ser_data_in, LdBr_Shft);
  or or_1 (or_1_out, and_1_out, and_2_out);
  and and_2 (and_2_out, not_1_out, I3);
  D_Flip_Flop d_ff_1 (.clk(clock_1_out), .D(or_1_out), .Q(Q3));  // open: Qn, preset, en, reset
  and and_3 (and_3_out, Q3, LdBr_Shft);
  and and_4 (and_4_out, not_1_out, I2);
  D_Flip_Flop d_ff_2 (.clk(clock_1_out), .D(or_2_out), .Q(Q2));  // open: Qn, preset, en, reset
  or or_2 (or_2_out, and_3_out, and_4_out);
  and and_5 (and_5_out, Q2, LdBr_Shft);
  and and_6 (and_6_out, not_1_out, I1);
  or or_3 (or_3_out, and_5_out, and_6_out);
  D_Flip_Flop d_ff_3 (.clk(clock_1_out), .D(or_3_out), .Q(Q1));  // open: Qn, preset, en, reset
  and and_7 (and_7_out, Q1, LdBr_Shft);
  or or_4 (or_4_out, and_7_out, and_8_out);
  and and_8 (and_8_out, not_1_out, I0);
  D_Flip_Flop d_ff_4 (.clk(clock_1_out), .D(or_4_out), .Q(Q0));  // open: Qn, preset, en, reset

  assign Serial_dataOut = Q0;
endmodule

module UniversalSftReg (
  input  Clear,
  input  [1:0] ModeControl,
  input  SerDataIn,
  input  SerIn_ShftLeft,
  input  I3,
  input  I2,
  input  I1,
  input  I0,
  output Q3,
  output Q2,
  output Q1,
  output Q0
);

  wire clock_1_out, multiplexer_1_out, multiplexer_2_out, multiplexer_3_out, multiplexer_4_out;

  Clock clock_1 (.out(clock_1_out));
  Multiplexer #(.select(2)) multiplexer_1 (
    .in0(Q3), .in1(SerDataIn), .in2(Q2), .in3(I3), .out(multiplexer_1_out), .sel(ModeControl));  // open: en
  D_Flip_Flop d_ff_1 (.clk(clock_1_out), .D(multiplexer_1_out), .Q(Q3), .reset(Clear));  // open: Qn, preset, en
  D_Flip_Flop d_ff_2 (.clk(clock_1_out), .D(multiplexer_2_out), .Q(Q2), .reset(Clear));  // open: Qn, preset, en
  Multiplexer #(.select(2)) multiplexer_2 (
    .in0(Q2), .in1(Q3), .in2(Q1), .in3(I2), .out(multiplexer_2_out), .sel(ModeControl));  // open: en
  Multiplexer #(.select(2)) multiplexer_3 (
    .in0(Q1), .in1(Q2), .in2(Q0), .in3(I1), .out(multiplexer_3_out), .sel(ModeControl));  // open: en
  D_Flip_Flop d_ff_3 (.clk(clock_1_out), .D(multiplexer_3_out), .Q(Q1), .reset(Clear));  // open: Qn, preset, en
  Multiplexer #(.select(2)) multiplexer_4 (
    .in0(Q0), .in1(Q1), .in2(SerIn_ShftLeft), .in3(I0), .out(multiplexer_4_out), .sel(ModeControl));  // open: en
  D_Flip_Flop d_ff_4 (.clk(clock_1_out), .D(multiplexer_4_out), .Q(Q0), .reset(Clear));  // open: Qn, preset, en
endmodule
