// Logisim project switch-level.circ as structural Verilog: 3 circuits, main circuit inverter
module inverter (
  input  in_1
);

  wire transistor_1_out;

  Transistor transistor_1 (.in(1'b1), .out(transistor_1_out), .gate(in_1));
  Transistor #(.\type ("n")) transistor_2 (.in(1'b0), .out(transistor_1_out), .gate(in_1));
  // Probe on transistor_1_out
endmodule

module \nand  (
  input  in_1,
  input  in_2
);

  wire transistor_1_out, transistor_3_out;

  Transistor transistor_1 (.in(1'b1), .out(transistor_1_out), .gate(in_1));
  Transistor #(.\type ("n")) transistor_2 (.in(transistor_3_out), .out(transistor_1_out), .gate(in_1));
  Transistor #(.\type ("n")) transistor_3 (.in(1'b0), .out(transistor_3_out), .gate(in_2));
  Transistor transistor_4 (.in(1'b1), .out(transistor_1_out), .gate(in_2));
  // Probe on transistor_1_out
endmodule

module \nor  (
  input  in_1,
  input  in_2
);

  wire transistor_1_out, transistor_2_out;

  Transistor transistor_1 (.in(1'b1), .out(transistor_1_out), .gate(in_1));
  Transistor transistor_2 (.in(transistor_1_out), .out(transistor_2_out), .gate(in_2));
  Transistor #(.\type ("n")) transistor_3 (.in(in_2), .out(transistor_2_out), .gate(in_1));
  // Probe on transistor_2_out
  Transistor #(.\type ("n")) transistor_4 (.in(in_2), .out(transistor_2_out), .gate(in_2));
  // also tied to GND on the sheet: in_2
endmodule
